# Fritzing sketch NucleoL4_HD44780_wiring (saved by Fritzing 0.9.2b)
breadboards: 1

parts:
  J1 = STM32 Nucleo boards
  LCD1 = LCD screen
  R1 = Rotary Potentiometer (Small) [maximum_resistance=100kΩ package=THT]

nets:
  N1: J1.A3, LCD1.DB4
  N2: J1.A4/SDA, LCD1.E
  5V: J1.5V, LCD1.VDD, LCD1.LED+, R1.leg2
  GND: J1.GND, LCD1.VSS, LCD1.R/W, LCD1.LED-, R1.leg1
  N3: J1.PB2, LCD1.DB6
  N4: J1.PB1, LCD1.DB5
  N5: J1.PB3, LCD1.DB7
  N6: J1.PC2, LCD1.RS
  N7: LCD1.V0, R1.wiper
